# Fritzing sketch LCD (saved by Fritzing 0.9.9b)
breadboards: 1

parts:
  GLCD_128x1 = 128 x 64 Graphic LCD
  R1 = Rotary Potentiometer (Small) [maximum_resistance=100kΩ package=THT]
  Componente1 = Arduino Uno (Rev3)
  R2 = Resistor [tolerance=±5% power=0.25 resistance=220 package=THT]

nets:
  N1: GLCD_128x1.1_Vss, GLCD_128x1.6_Enable, GLCD_128x1.20_K(-), R1.leg1, R1.leg2, Componente1.GND, R2.Pin_0
  N2: GLCD_128x1.2_Vdd, GLCD_128x1.19_A(+), Componente1.5V
  N3: GLCD_128x1.3_Vo, R2.Pin_1
  N4: GLCD_128x1.4_D/I, Componente1.D1/TX
  N5: GLCD_128x1.5_R/W, Componente1.D2
  N6: GLCD_128x1.11_DB4, Componente1.D4
  N7: GLCD_128x1.12_DB5, Componente1.D5_PWM
  N8: GLCD_128x1.13_DB6, Componente1.D6_PWM
  N9: GLCD_128x1.14_DB7, Componente1.D7
